# Fritzing sketch aqi_mon (saved by Fritzing 0.9.3b)

parts:
  Part1 = Adafruit SHT31-D Sensirion Temperature/Humidity Sensor [part_number="Adafruit #2857"]
  Part2 = Adafruit HUZZAH32 ESP32 Feather [part_number="Adafruit #3405"]
  Part3 = Adafruit CCS811

nets:
  VIN: Part1.VIN, Part2.VBUS, Part3.VIN
  GND: Part1.GND, Part2.GND, Part3.GND
  N1: Part1.SCL, Part2.SCL, Part3.SCL
  N2: Part1.SDA, Part2.SDA, Part3.SDA
  3.3V: Part2.3.3V, Part3.3.3V, Part3.!WAKE

custom parts:
  Adafruit SHT31-D Sensirion Temperature/Humidity Sensor: Sensirion Temperature/Humidity sensors are some of the finest & highest-accuracy devices you can get. And, finally we have some that have a true I2C interface for easy reading. The SHT31-D sensor has an excellent ±2% relative humidity and ±0.3°C accuracy for most uses. Unlike earlier SHT sensors, this sensor has a true I2C interface, and (bonus!) even with two address options. It also is 3V or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
